# Fritzing sketch DHT sensor control RGB LED (saved by Fritzing 0.9.4)
breadboards: 1

parts:
  Part1 = Arduino Uno (Rev3)
  RHT1 = Humidity and Temperature Sensor RHT03
  R1 = Resistor [tolerance=±5% resistance=10k package=THT]
  LED2 = RGB LED (com. cathode, rgb) [package="5 mm [THT]"]

nets:
  N1: Part1.D11_PWM/MOSI, LED2.green_anode
  N2: Part1.D2, RHT1.Data-signal, R1.Pin_0
  5V: Part1.5V, RHT1.Vcc, LED2.red_anode
  N3: Part1.GND, RHT1.GND_1, R1.Pin_1, LED2.common_cathode
